# Fritzing sketch SmartMiniCamper (saved by Fritzing 0.9.3b)
breadboards: 2

parts:
  IC1 = MCP3008 8-channel 10-bit ADC [part_number=MCP3008]
  RaspberryPi1 = Raspberry Pi Model B
  Part4 = ACS712 Low Current Sensor Board v12
  VCC1 = Battery block 9V
  D1 = SOLAR-IXYS [package=solarbit-12x1]
  Part5 = ACS712 Low Current Sensor Board v12
  U1 = V_REG_NCP50X [package=dpak-5]

nets:
  N1: IC1.no_name_yet#1, Part4.VO
  N2: IC1.no_name_yet#2, Part5.VO
  N3: IC1.no_name_yet#3, U1.EN
  GND: IC1.no_name_yet#4, IC1.no_name_yet#5, IC1.no_name_yet#6, IC1.no_name_yet#7, IC1.no_name_yet#8, IC1.no_name_yet#9, IC1.no_name_yet#14, RaspberryPi1.GND, Part4.GND, Part5.GND, U1.GND
  N4: IC1.no_name_yet#10, RaspberryPi1.CS0
  N5: IC1.no_name_yet#11, RaspberryPi1.MOSI
  N6: IC1.no_name_yet#12, RaspberryPi1.MISO
  N7: IC1.no_name_yet#13, RaspberryPi1.SCLK
  N8: IC1.no_name_yet#15, IC1.no_name_yet#16, RaspberryPi1.3V3, U1.ADJ
  5V: RaspberryPi1.5V, Part4.5V, Part5.5V
  N9: Part4.IP+, D1.A
  N10: Part4.IP-, VCC1.+, Part5.IP+, U1.IN
  N11: VCC1.-, U1.OUT

notes:
  Verbraucher
  Spannungssensor
  Stromstärkesensoren
  Solar Laderegler PEKO10

custom parts:
  Raspberry Pi Model B: Raspberry Pi (Model B)
